# Fritzing sketch CD4027Test (saved by Fritzing 0.9.10b)
breadboards: 1

parts:
  Part1 = Arduino Uno (Rev3) - ICSP
  CD1 = CD4027 [part_number=CD4027 package="DIP (Dual Inline) [THT]"]
  C1 = Ceramic Capacitor [capacitance=100nF voltage=35V package="200 mil [THT, multilayer]"]

nets:
  GND: Part1.GND, CD1.VSS, C1.0
  N1: Part1.D8, CD1.~Q1
  N2: Part1.D9_PWM, CD1.Q1
  N3: Part1.D3_PWM, CD1.SET1
  N4: Part1.D4, CD1.J1
  N5: Part1.D5_PWM, CD1.K1
  N6: Part1.D6_PWM, CD1.RESET1
  N7: Part1.D7, CD1.CLOCK1
  5V: Part1.5V, CD1.VDD, C1.1

custom parts:
  CD4027: CMOS Dual J-K Flip Flop
