# Fritzing sketch ShifterTest (saved by Fritzing 0.9.10b)
breadboards: 1

parts:
  U1 = 74HC595 [package="DIP16 [THT]"]
  LED1 = LED - 5mm [color="Red (633nm)" current=0.030 package="5 mm [THT]"]
  LED2 = LED - 5mm [color="Red (633nm)" current=0.030 package="5 mm [THT]"]
  LED3 = LED - 5mm [color="Red (633nm)" current=0.030 package="5 mm [THT]"]
  R1 = Bussed Resistor-4 (SIP-5) [tolerance=±5% resistance=220 package=SIP-5]
  R2 = Bussed Resistor-4 (SIP-5) [tolerance=±5% resistance=220 package=SIP-5]
  LED4 = LED - 5mm [color="Red (633nm)" current=0.030 package="5 mm [THT]"]
  LED5 = LED - 5mm [color="Green (555nm)" current=0.030 package="5 mm [THT]"]
  LED6 = LED - 5mm [color="Green (555nm)" current=0.030 package="5 mm [THT]"]
  LED7 = LED - 5mm [color="Green (555nm)" current=0.030 package="5 mm [THT]"]
  LED9 = LED - 5mm [color="Green (555nm)" current=0.030 package="5 mm [THT]"]
  U3 = attiny85 [package=dip]

nets:
  N1: U1.Q1, LED6.anode
  N2: U1.Q2, LED2.anode
  N3: U1.Q3, LED9.anode
  N4: U1.Q4, LED1.anode
  N5: U1.Q5, LED7.anode
  N6: U1.Q6, LED3.anode
  N7: U1.Q7, LED5.anode
  N8: U1.GND, U1.OE, R1.Pin_0, R2.Pin_0, U3.Pin_4
  N9: U1.MR, U1.VCC, U3.Pin_8
  N10: U1.SH_CP, U3.Pin_5
  N11: U1.ST_CP, U3.Pin_6
  N12: U1.DS, U3.Pin_7
  N13: U1.Q0, LED4.anode
  N14: LED1.cathode, R1.Pin_4
  N15: LED2.cathode, R2.Pin_2
  N16: LED3.cathode, R1.Pin_2
  N17: R1.Pin_1, LED5.cathode
  N18: R1.Pin_3, LED7.cathode
  N19: R2.Pin_1, LED9.cathode
  N20: R2.Pin_3, LED6.cathode
  N21: R2.Pin_4, LED4.cathode

custom parts:
  Bussed Resistor-4 (SIP-5): A resistor array is a single package which contains more than one resistor. They are typically used for convenience when several resistors are needed together in the same place in a circuit.
