# Fritzing sketch TIL311ShifterTest (saved by Fritzing 0.9.10b)
breadboards: 2

parts:
  U1 = 74HC595 [package="DIP16 [THT]"]
  U3 = attiny85 [package=dip]
  DS1 = TIL311 [package="DIP (Dual Inline)"]

nets:
  N1: U1.Q1, DS1.B
  N2: U1.Q2, DS1.C
  N3: U1.Q3, DS1.D
  GND: U1.GND, U1.OE, U3.Pin_4, DS1.ST, DS1.GND
  VCC: U1.MR, U1.VCC, U3.Pin_8, DS1.+5V, DS1.VCC
  N4: U1.SH_CP, U3.Pin_5
  N5: U1.ST_CP, U3.Pin_6
  N6: U1.DS, U3.Pin_7
  N7: U1.Q0, DS1.A
  N8: U3.Pin_2, DS1.BL

custom parts:
  TIL311: Display a matrice di punti esadecimale
